# Fritzing sketch OUT_Rly_1 (saved by Fritzing 0.9.3b)
breadboards: 2

parts:
  KY-1 = Keyes Relay [package=THT]
  Part3 = Lilypad Battery Connect
  LED3 = LEDs [package=led10mm]
  Part4 = Arduino Uno (Rev3) - ICSP
  U1 = Voltage Regulator - 5V [package="TO220 [THT]"]
  VCC1 = Battery block 9V

nets:
  N1: KY-1.signal, Part4.D7
  N2: KY-1.power, U1.output_voltage
  GND: KY-1.ground, Part4.GND, U1.GND, VCC1.-
  N3: KY-1.C, Part3.-
  N4: KY-1.NO, LED3.C
  N5: Part3.+, LED3.A
  N6: U1.input_voltage, VCC1.+

notes:
  Lamp
  voltage Regulator LM7805
  Relay module
  220v socket

custom parts:
  Keyes Relay: The Keyes 5V relay module is suitable for SCM development, home appliance control. It uses a 5V~12V TIL control signal which can control DC / AC signal.
