# Fritzing sketch Rly_SW_on-off (saved by Fritzing 0.9.3b)
breadboards: 1

parts:
  KY-1 = Keyes Relay [package=THT]
  Part3 = Lilypad Battery Connect
  LED3 = LEDs [package=led10mm]
  Part4 = Arduino Uno (Rev3) - ICSP
  U1 = Voltage Regulator - 5V [package="TO220 [THT]"]
  VCC1 = Battery block 9V
  KY-2 = Keyes Relay [package=THT]
  KY-3 = Keyes Relay [package=THT]
  KY-4 = Keyes Relay [package=THT]
  L3 = Solenoid
  M1 = DC Motor
  LED4 = smd LED [color="Red (633nm)" package="0805 [SMD]"]
  VCC4 = Battery
  VCC5 = Battery
  VCC6 = Battery block 9V
  R1 = Resistor [tolerance=±5% resistance=10k package=THT]
  S1 = Pushbutton [package="[THT]"]
  S2 = Pushbutton [package="[THT]"]
  S3 = Pushbutton [package="[THT]"]
  S4 = Pushbutton [package="[THT]"]
  R2 = Resistor [tolerance=±5% resistance=10k package=THT]
  R3 = Resistor [tolerance=±5% resistance=10k package=THT]
  R4 = Resistor [tolerance=±5% resistance=10k package=THT]

nets:
  N1: KY-1.signal, Part4.D8
  N2: KY-1.power, KY-2.power, KY-3.power, KY-4.power
  N3: KY-1.ground, KY-2.ground, KY-3.ground, KY-4.ground
  N4: KY-1.C, L3.pin1
  N5: KY-1.NO, VCC6.-
  N6: Part3.-, KY-4.C
  N7: Part3.+, LED3.C
  N8: LED3.A, KY-4.NO
  N9: Part4.D9_PWM, KY-4.signal
  GND: Part4.GND, U1.GND, VCC1.-, R1.Pin_1, R2.Pin_1, R3.Pin_1, R4.Pin_1
  N10: Part4.D2, R1.Pin_0, S1.Pin_1, S1.Pin_2
  N11: Part4.D3_PWM, S2.Pin_1, S2.Pin_2, R2.Pin_0
  N12: Part4.D4, S3.Pin_1, S3.Pin_2, R3.Pin_0
  N13: Part4.D5_PWM, S4.Pin_1, S4.Pin_2, R4.Pin_0
  N14: Part4.D6_PWM, KY-3.signal
  N15: Part4.D7, KY-2.signal
  N16: U1.input_voltage, VCC1.+
  N17: U1.output_voltage, S1.Pin_3, S1.Pin_4, S2.Pin_3, S2.Pin_4, S3.Pin_3, S3.Pin_4, S4.Pin_3, S4.Pin_4
  N18: KY-2.C, VCC4.-
  N19: KY-2.NO, M1.pin_1
  N20: KY-3.C, VCC5.-
  N21: KY-3.NO, LED4.cathode
  N22: L3.pin2, VCC6.+

notes:
  Device 1: Lamp 220v
  voltage Regulator LM7805
  Relay module 4ch.
  220v socket
  Device 2: DC motor 9v
  Device 3: DC motor 3v
  Device 4: LED
  1 2 3 4

custom parts:
  Keyes Relay: The Keyes 5V relay module is suitable for SCM development, home appliance control. It uses a 5V~12V TIL control signal which can control DC / AC signal.
