# Fritzing sketch KeyP_LCD_Rly_pswrd   1 (saved by Fritzing 0.9.3b)
breadboards: 2

parts:
  KY-1 = Keyes Relay [package=THT]
  U1 = Voltage Regulator - 5V [package="TO220 [THT]"]
  VCC1 = Battery block 9V
  Part4 = Arduino Uno (Rev3) - ICSP
  U4 = LCD-16X2 [package=lcd-16x2]
  Matrix_keypad1 = KEYPAD 4x4
  R1 = Resistor [tolerance=±5% resistance=1k package="0603 [SMD]"]
  R2 = Resistor [tolerance=±5% resistance=1k package="0603 [SMD]"]
  L2 = Solenoid
  BAT1 = BC9VPC [package=bc9vpc]

nets:
  N1: KY-1.signal, Part4.D2
  N2: KY-1.power, U1.output_voltage, U4.VDD, R1.Pin_0
  GND: KY-1.ground, U1.GND, VCC1.-, Part4.GND, U4.VSS, U4.R_W, U4.K, R2.Pin_0
  N3: KY-1.C, L2.pin2
  N4: KY-1.NO, BAT1.V+
  N5: U1.input_voltage, VCC1.+
  N6: Part4.A0, U4.RS
  N7: Part4.A1, U4.E
  N8: Part4.A2, U4.DB4
  N9: Part4.A3, U4.DB5
  N10: Part4.A4/SDA, U4.DB6
  N11: Part4.A5/SCL, U4.DB7
  N12: Part4.ICSP_MOSI, Part4.D11_PWM/MOSI, Matrix_keypad1.col1
  N13: Part4.D8, Matrix_keypad1.col4
  N14: Part4.D9_PWM, Matrix_keypad1.col3
  N15: Part4.D10_PWM/SS, Matrix_keypad1.col2
  N16: Part4.D4, Matrix_keypad1.row4
  N17: Part4.D5_PWM, Matrix_keypad1.row3
  N18: Part4.D6_PWM, Matrix_keypad1.row2
  N19: Part4.D7, Matrix_keypad1.row1
  N20: U4.VO, R2.Pin_1
  N21: U4.A, R1.Pin_1

notes:
  Fan motor
  voltage Regulator LM7805
  Relay module
  Fan supply
  LCD 2x16
  Keypad 4x4

custom parts:
  Keyes Relay: The Keyes 5V relay module is suitable for SCM development, home appliance control. It uses a 5V~12V TIL control signal which can control DC / AC signal.
  KEYPAD 4x4: Matrix keypad 16 buttons, 4 rows x 4 columns
