# Fritzing sketch application_1 (saved by Fritzing 0.9.3b)
breadboards: 2

parts:
  KY-1 = Keyes Relay [package=THT]
  IR1 = TSOP312.., 314.. [package=THT]
  Part3 = Lilypad Battery Connect
  LED3 = LEDs [package=led10mm]
  Part4 = Arduino Uno (Rev3) - ICSP
  U1 = Voltage Regulator - 5V [package="TO220 [THT]"]
  U3 = SWITCH_SPDT [package=kps-1290]
  VCC1 = Battery block 9V

nets:
  N1: KY-1.signal, Part4.D6_PWM
  N2: KY-1.power, IR1.Vs, U1.output_voltage
  GND: KY-1.ground, IR1.GND, Part4.GND, U1.GND, VCC1.-
  N3: KY-1.NC, U3.O
  N4: KY-1.C, Part3.-
  N5: KY-1.NO, U3.S
  N6: IR1.Data, Part4.D11_PWM/MOSI
  N7: Part3.+, LED3.A
  N8: LED3.C, U3.P
  N9: U1.input_voltage, VCC1.+

notes:
  Lamp
  3 pin SW
  voltage Regulator LM7805
  Relay module
  IR receiver
  220v socket

custom parts:
  Keyes Relay: The Keyes 5V relay module is suitable for SCM development, home appliance control. It uses a 5V~12V TIL control signal which can control DC / AC signal.
